// Logisim project lab4p1.circ as structural Verilog: 1 circuit, main circuit main
module main (
  input  in_1,
  input  in_2,
  input  in_3,
  input  in_4,
  input  in_5,
  input  in_6
);

  wire and_1_out, and_2_out, nand_1_out, nand_2_out, nand_3_out, nand_4_out, nand_5_out, not_1_out,
       not_2_out, or_1_out;

  not not_1 (not_1_out, in_2);
  not not_2 (not_2_out, in_3);
  nand nand_1 (nand_1_out, in_5, in_5);
  nand nand_2 (nand_2_out, in_4, nand_1_out, in_6);
  nand nand_3 (nand_3_out, in_6, in_6);
  and and_1 (and_1_out, in_1, not_1_out, in_3);
  and and_2 (and_2_out, in_2, not_2_out, not_2_out);
  nand nand_4 (nand_4_out, nand_3_out, in_5);
  nand nand_5 (nand_5_out, nand_2_out, nand_4_out);
  or or_1 (or_1_out, and_1_out, and_2_out);
  LED led_1 (.in(nand_5_out));
  LED led_2 (.in(or_1_out));
endmodule
