// Logisim project lab8p1.circ as structural Verilog: 1 circuit, main circuit main
module main (
  output out_1,
  output out_2
);

  Clock clock_1 (.out(out_1));
  not not_1 (out_2, out_1);
endmodule
