// Logisim project lab8p2v2.circ as structural Verilog: 1 circuit, main circuit main
module main (
);

  wire and_1_out, clock_1_out, j_k_ff_1_q, j_k_ff_2_q, s_r_ff_1_q, s_r_ff_1_qn;

  Clock clock_1 (.out(clock_1_out));
  and and_1 (and_1_out, s_r_ff_1_q, j_k_ff_2_q);
  J_K_Flip_Flop j_k_ff_1 (
    .J(and_1_out), .clk(clock_1_out), .K(and_1_out), .Q(j_k_ff_1_q));  // open: Qn, preset, en, reset
  J_K_Flip_Flop j_k_ff_2 (
    .J(s_r_ff_1_q), .clk(clock_1_out), .K(s_r_ff_1_q), .Q(j_k_ff_2_q));  // open: Qn, preset, en, reset
  S_R_Flip_Flop s_r_ff_1 (
    .S(s_r_ff_1_qn), .clk(clock_1_out), .R(s_r_ff_1_q), .Q(s_r_ff_1_q), .Qn(s_r_ff_1_qn));  // open: preset, reset, en
endmodule
