// Logisim project lab8p3.circ as structural Verilog: 1 circuit, main circuit main
module main (
);

  wire button_1_out, button_2_out, button_3_out, button_4_out, button_5_out, button_6_out, clock_1_out,
       nand_1_out, nand_2_out, nand_3_out, nand_4_out, s_r_ff_1_q, s_r_ff_1_qn, s_r_ff_2_q, s_r_ff_2_qn,
       s_r_ff_3_q, s_r_ff_3_qn;

  Button button_1 (.out(button_1_out));
  Button button_2 (.out(button_2_out));
  Button button_3 (.out(button_3_out));
  Button button_4 (.out(button_4_out));
  Button button_5 (.out(button_5_out));
  Button button_6 (.out(button_6_out));
  Clock clock_1 (.out(clock_1_out));
  S_R_Flip_Flop s_r_ff_1 (
    .S(button_1_out), .clk(clock_1_out), .R(button_2_out), .Q(s_r_ff_1_q), .Qn(s_r_ff_1_qn));  // open: preset, reset, en
  S_R_Flip_Flop s_r_ff_2 (
    .S(button_3_out), .clk(clock_1_out), .R(button_4_out), .Q(s_r_ff_2_q), .Qn(s_r_ff_2_qn));  // open: preset, reset, en
  S_R_Flip_Flop s_r_ff_3 (
    .S(button_5_out), .clk(clock_1_out), .R(button_6_out), .Q(s_r_ff_3_q), .Qn(s_r_ff_3_qn));  // open: preset, reset, en
  nand nand_1 (nand_1_out, s_r_ff_1_q, s_r_ff_2_qn);
  nand nand_2 (nand_2_out, s_r_ff_2_q, s_r_ff_3_qn);
  nand nand_3 (nand_3_out, s_r_ff_1_qn, s_r_ff_3_q);
  nand nand_4 (nand_4_out, nand_1_out, nand_2_out, nand_3_out);
endmodule
