// Logisim project lab8p4.circ as structural Verilog: 1 circuit, main circuit main
module main (
);

  wire button_1_out, button_2_out, button_3_out, button_4_out, button_5_out, button_6_out, clock_1_out,
       nor_1_out, nor_2_out, nor_3_out, nor_4_out, nor_5_out, s_r_ff_1_q, s_r_ff_1_qn, s_r_ff_2_q,
       s_r_ff_2_qn, s_r_ff_3_q, s_r_ff_3_qn;

  Button button_1 (.out(button_1_out));
  Button button_2 (.out(button_2_out));
  Button button_3 (.out(button_3_out));
  Button button_4 (.out(button_4_out));
  Button button_5 (.out(button_5_out));
  Button button_6 (.out(button_6_out));
  Clock clock_1 (.out(clock_1_out));
  S_R_Flip_Flop s_r_ff_1 (
    .S(button_1_out), .clk(clock_1_out), .R(button_2_out), .Q(s_r_ff_1_q), .Qn(s_r_ff_1_qn));  // open: preset, reset, en
  S_R_Flip_Flop s_r_ff_2 (
    .S(button_3_out), .clk(clock_1_out), .R(button_4_out), .Q(s_r_ff_2_q), .Qn(s_r_ff_2_qn));  // open: preset, reset, en
  S_R_Flip_Flop s_r_ff_3 (
    .S(button_5_out), .clk(clock_1_out), .R(button_6_out), .Q(s_r_ff_3_q), .Qn(s_r_ff_3_qn));  // open: preset, reset, en
  nor nor_1 (nor_1_out, s_r_ff_1_qn, s_r_ff_2_q);
  nor nor_2 (nor_2_out, s_r_ff_2_qn, s_r_ff_3_q);
  nor nor_3 (nor_3_out, s_r_ff_1_q, s_r_ff_3_qn);
  nor nor_4 (nor_4_out, nor_1_out, nor_2_out, nor_3_out);
  nor nor_5 (nor_5_out, nor_4_out, nor_4_out);
endmodule
