// Logisim project lab9p2.circ as structural Verilog: 1 circuit, main circuit main
module main (
  input  [3:0] in_1,
  input  in_2
);

  wire and_1_out, and_2_out, clock_1_out, not_1_out;
  wire [3:0] adder_1_out, j_k_ff_4_q;
  wire [7:0] ram_1_data, rom_1_data;

  Clock clock_1 (.out(clock_1_out));
  and and_1 (and_1_out, j_k_ff_4_q[2], j_k_ff_4_q[0], j_k_ff_4_q[1]);
  J_K_Flip_Flop j_k_ff_1 (
    .J(and_1_out), .clk(clock_1_out), .K(and_1_out), .Q(j_k_ff_4_q[3]));  // open: Qn, preset, en, reset
  and and_2 (and_2_out, j_k_ff_4_q[0], j_k_ff_4_q[1]);
  J_K_Flip_Flop j_k_ff_2 (
    .J(and_2_out), .clk(clock_1_out), .K(and_2_out), .Q(j_k_ff_4_q[2]));  // open: Qn, preset, en, reset
  J_K_Flip_Flop j_k_ff_3 (
    .J(j_k_ff_4_q[0]), .clk(clock_1_out), .K(j_k_ff_4_q[0]), .Q(j_k_ff_4_q[1]));  // open: Qn, preset, en, reset
  Adder #(.width(4)) adder_1 (.a(j_k_ff_4_q), .b(in_1), .out(adder_1_out));  // open: cin, cout
  J_K_Flip_Flop j_k_ff_4 (
    .J(clock_1_out), .clk(clock_1_out), .K(clock_1_out), .Q(j_k_ff_4_q[0]));  // open: Qn, preset, en, reset
  ROM #(.addrWidth(4)) rom_1 (.addr(j_k_ff_4_q), .data(rom_1_data));  // open: sel
  RAM #(.addrWidth(4)) ram_1 (.addr(adder_1_out), .data(ram_1_data), .clk(clock_1_out), .ld(in_2));  // open: sel, clr
  not not_1 (not_1_out, in_2);
  assign ram_1_data = not_1_out ? rom_1_data : 8'bz;  // Controlled_Buffer controlled_buffer_1
  DotMatrix #(.matrixcols(8), .matrixrows(1)) dotmatrix_1 (
    .col0(ram_1_data[7]), .col1(ram_1_data[6]), .col2(ram_1_data[5]), .col3(ram_1_data[4]),
    .col4(ram_1_data[3]), .col5(ram_1_data[2]), .col6(ram_1_data[1]), .col7(ram_1_data[0]));

  // Notes on the sheet:
  //   contents of rom_1 (hex, n*v repeats v):
  //   2 4 6 8 10 12 14 16 18 20
endmodule
